# Fritzing sketch power_board (saved by Fritzing 0.8.5b)
circuit board: 6.99588cm x 4.40672cm

parts:
  R3 = Resistor [tolerance=±5% resistance=220 package=THT]
  U1 = 555 Timer [package="DIP8 [THT]"]
  X1 = USB Connectors [package=usb-a-s-silk-female]
  RPI_GPIO = double row male pin header, 26 pins [form="♂ (male)"]
  D2 = Rectifier Diode [part_number=1N4001 package="300 mil [THT]"]
  U2 = mystery part, 24 pins [chip_label=?]
  Q1 = NPN-Transistor [package="TO92 [THT]"]
  R2 = Resistor [tolerance=±5% resistance=1k package=THT]
  R1 = Resistor [tolerance=±5% resistance=47k package=THT]
  INPUT = screw terminal, 4 pins
  OUTPUT = screw terminal, 4 pins

nets:
  N1: R3.Pin_0, U1.Reset, D2.cathode
  N2: R3.Pin_1, U1.Output, U2.pin1
  GND: U1.Ground, X1.GND
  N3: U1.Control_Voltage, U1.Discharge, R2.Pin_0
  N4: U1.Vcc_Supply_Voltage, U2.pin22, U2.pin23, INPUT.pin1, OUTPUT.pin1
  N5: X1.VBUS, U2.pin14, OUTPUT.pin3
  N6: RPI_GPIO.pin6, U2.pin2, U2.pin3, U2.pin16, Q1.E, INPUT.pin4, OUTPUT.pin4
  N7: RPI_GPIO.pin16, Q1.C
  N8: RPI_GPIO.pin17, R2.Pin_1
  N9: D2.anode, R1.Pin_0, INPUT.pin2, OUTPUT.pin2
  N10: Q1.B, R1.Pin_1
